# Fritzing sketch op07 (saved by Fritzing 0.9.5d)
breadboards: 1

parts:
  IC1 = IC, DIP package, 8 pins [chip_label=OP-07]
  R1 = Resistor [tolerance=±5% resistance=220 package=THT]
  R2 = Resistor [tolerance=±5% resistance=220 package=THT]
  C1 = Ceramic Capacitor [capacitance=100nF package="100 mil [THT, multilayer]"]
  C2 = Ceramic Capacitor [capacitance=100nF package="100 mil [THT, multilayer]"]
  C3 = Ceramic Capacitor [capacitance=100nF package="100 mil [THT, multilayer]"]
  C4 = Ceramic Capacitor [capacitance=100nF package="100 mil [THT, multilayer]"]

nets:
  N1: IC1.pin2, IC1.pin6, R1.Pin_1, R2.Pin_0
  N2: IC1.pin4, C1.1, C2.1
  N3: IC1.pin7, C3.1, C4.1
  N4: C1.0, C2.0
  N5: C3.0, C4.0
