# Fritzing sketch tl081 (saved by Fritzing 0.9.5d)
breadboards: 1

parts:
  IC3 = IC, DIP package, 8 pins [chip_label=TL081]
  C9 = Ceramic Capacitor [capacitance=100nF package="100 mil [THT, multilayer]"]
  C10 = Ceramic Capacitor [capacitance=100nF package="100 mil [THT, multilayer]"]
  C11 = Ceramic Capacitor [capacitance=100nF package="100 mil [THT, multilayer]"]
  C12 = Ceramic Capacitor [capacitance=100nF package="100 mil [THT, multilayer]"]
  R4 = Resistor [tolerance=±5% resistance=220 package=THT]
  R5 = Resistor [tolerance=±5% resistance=220 package=THT]

nets:
  N1: IC3.pin2, IC3.pin6
  N2: IC3.pin3, R4.Pin_1, R5.Pin_0
  N3: IC3.pin4, C9.1, C10.1
  N4: IC3.pin7, C11.1, C12.1
  N5: C9.0, C10.0
  N6: C11.0, C12.0
