# Fritzing sketch 555 (saved by Fritzing 0.9.5d)
breadboards: 1

parts:
  U1 = 555 Timer [package="SO8 [SMD]"]  # not connected
  C2 = Ceramic Capacitor [capacitance="100 nF" package="1206 [SMD, multilayer]"]
  C1 = Tantalum Capacitor [capacitance=1μF package="200 mil [THT, tantalum]"]  # not connected
  R1 = Resistor [tolerance=±5% resistance=220 package="0402 [SMD]"]
  R2 = Resistor [tolerance=±5% resistance=220 package="0402 [SMD]"]
  LED1 = smd LED [color="Red (633nm)" package="0805 [SMD]"]
  R3 = Resistor [tolerance=±5% resistance=220 package="0402 [SMD]"]

nets:
  N1: C2.0, R2.Pin_0
  N2: C2.1, R3.Pin_0
  N3: R1.Pin_0, R2.Pin_1
  N4: LED1.anode, R3.Pin_1
