# Fritzing sketch offset inverted amplifier (saved by Fritzing 0.9.5d)
breadboards: 1

parts:
  R1 = Resistor [tolerance=±5% resistance=220 package="0402 [SMD]"]
  R2 = Resistor [tolerance=±5% resistance=220 package="0402 [SMD]"]
  IC2 = Dual Op-Amp [package=dip08]
  R3 = Resistor [tolerance=±5% resistance=220 package="0402 [SMD]"]
  R4 = Resistor [tolerance=±5% resistance=220 package="0402 [SMD]"]

nets:
  N1: R1.Pin_0, R2.Pin_1
  N2: R1.Pin_1, IC2.Vin--
  N3: R2.Pin_0, IC2.Vout
  N4: IC2.Vin+, R3.Pin_0, R4.Pin_0
  N5: IC2.Vss, R4.Pin_1

notes:
  [write your note here]r
  write your note here]

custom parts:
  Dual Op-Amp: Generic op-amp footprint
